# Fritzing sketch Current_ADC (saved by Fritzing 0.9.3b)
circuit board: 2.36136cm x 3.77051cm
breadboards: 1

parts:
  Part2 = Adafruit ADS1115 16Bit I2C ADC [part_number="Adafruit #1085"]
  ACS712_Current_Sensor2 = ACS712 Current Sensor
  J2 = double row female pin header, 6 pins [form="♀ (female)"]

nets:
  N1: Part2.AIN0, ACS712_Current_Sensor2.OUT
  N2: Part2.SDA, J2.pin2
  N3: Part2.SCL, J2.pin3
  GND: Part2.GND, ACS712_Current_Sensor2.GND, J2.pin4
  VDD: Part2.VDD, ACS712_Current_Sensor2.VCC, J2.pin1

notes:
  Ahmad El-Hajj

custom parts:
  Adafruit ADS1115 16Bit I2C ADC: For microcontrollers without an analog-to-digital converter or when you want a higher-precision ADC, the ADS1115 provides 16-bit precision at 860 samples/second over I2C. The chip can be configured as 4 single-ended input channels, or two differential channels. As a nice bonus, it even includes a programmable gain amplifier, up to x16, to help boost up smaller single/differential signals to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
  ACS712 Current Sensor: A breakout board for the Allegro ACS712 is a Hall Effect-based linear current sensor. The module operates at 5V.
