# Fritzing sketch Current_ADCV2 (saved by Fritzing 0.9.3b)
circuit board: 2.66227cm x 3.45709cm
breadboards: 1

parts:
  Part2 = Adafruit ADS1115 16Bit I2C ADC [part_number="Adafruit #1085"]
  J2 = double row female pin header, 6 pins [form="♀ (female)"]
  J3 = female pin header, 3 pins [form="♀ (female)"]

nets:
  N1: Part2.AIN0, J3.pin2
  N2: Part2.SDA, J2.pin5
  N3: Part2.SCL, J2.pin6
  N4: Part2.GND, J2.pin1, J3.pin1
  N5: Part2.VDD, J2.pin4, J3.pin3

notes:
  Ahmad El-Hajj

custom parts:
  Adafruit ADS1115 16Bit I2C ADC: For microcontrollers without an analog-to-digital converter or when you want a higher-precision ADC, the ADS1115 provides 16-bit precision at 860 samples/second over I2C. The chip can be configured as 4 single-ended input channels, or two differential channels. As a nice bonus, it even includes a programmable gain amplifier, up to x16, to help boost up smaller single/differential signals to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
